// Logisim project CPU.circ as structural Verilog: 2 circuits, main circuit main
module main (
  input  RST
);

  wire ADD, ADDI, and_1_out, and_2_out, CLK, COUT, decoder_2_out1, decoder_2_out2, decoder_2_out3,
       decoder_2_out4, IN_P, IS_ALU, JC, JUMP, JZ, LOAD, MOV, MOVI, NOP, or_1_out, or_2_out, OUT_P, PC_INC,
       RAM_WRITE, REG_SET, ROTLI, ROTRI, SEL0, SEL1, SHLI, SHRI, STORE, SUB, SUBI, ZERO;
  wire [4:0] bit_extender_1_out, REG_ADDR, REGY;
  wire [5:0] and_3_out, bit_extender_2_out, OPCODE, subtractor_1_out;
  wire [15:0] A_q, adder_1_out, ALU_OUT, B, B_q, C_q, D_q, IMM16, multiplexer_1_out, PC, RAM_ADDR, RAM_IN,
       RAM_OUT, REG_IN, REG_OUT, REGX_OUT, REGY_OUT;
  wire [31:0] rom_1_data;

  Clock clock_1 (.out(CLK));
  Adder #(.width(16)) adder_1 (.a(PC), .b(16'h1), .out(adder_1_out));  // open: cin, cout
  // Probe on PC
  Multiplexer #(.width(16)) multiplexer_1 (.in0(IMM16), .in1(adder_1_out), .out(multiplexer_1_out), .sel(PC_INC));
  and and_1 (and_1_out, JZ, ZERO);
  and and_2 (and_2_out, JC, COUT);
  ROM #(.addrWidth(16), .dataWidth(32)) rom_1 (.addr(PC), .data(rom_1_data));
  RAM #(.addrWidth(16), .dataWidth(16)) ram_1 (
    .addr(RAM_ADDR), .we(RAM_WRITE), .oe(CLK), .din(RAM_IN), .dout(RAM_OUT));  // open: clk
  Register #(.width(16)) register_1 (.D(multiplexer_1_out), .en(1'b1), .clk(CLK), .Q(PC), .clr(RST));
  or or_1 (or_1_out, JUMP, and_1_out, and_2_out);
  not not_1 (PC_INC, or_1_out);
  Bit_Extender #(.in_width(6), .out_width(5)) bit_extender_1 (.in(OPCODE), .out(bit_extender_1_out));
  Decoder #(.select(5)) decoder_1 (
    .out0(NOP), .out4(SHRI), .out5(SHLI), .out6(ROTRI), .out7(ROTLI), .out8(ADD), .out9(SUB), .out12(ADDI),
    .out13(SUBI), .out16(LOAD), .out17(STORE), .out18(IN_P), .out19(OUT_P), .out20(JUMP), .out21(JZ),
    .out22(JC), .out23(MOV), .out24(MOVI), .sel(bit_extender_1_out), .en(1'b1));  // open: out1, out2, out3, out10, out11, out14, out15, out25, out26, out27, out28, out29, out30, out31
  // Probe on bit_extender_1_out
  // Probe on rom_1_data
  // Probe on OPCODE
  or or_2 (or_2_out, ADDI, SUBI);
  Decoder #(.select(5)) decoder_2 (
    .out1(decoder_2_out1), .out2(decoder_2_out2), .out3(decoder_2_out3), .out4(decoder_2_out4),
    .sel(REG_ADDR), .en(REG_SET));  // open: out0, out5, out6, out7, out8, out9, out10, out11, out12, out13, out14, out15, out16, out17, out18, out19, out20, out21, out22, out23, out24, out25, out26, out27, out28, out29, out30, out31
  assign bit_extender_2_out = {{5{or_2_out}}, or_2_out};  // Bit_Extender bit_extender_2
  assign and_3_out = bit_extender_2_out & 6'b000100;  // AND_Gate and_3, 6 bits wide
  Register #(.width(32)) register_2 (
    .D(rom_1_data), .en(1'b1), .clk(CLK), .Q({OPCODE, REG_ADDR, REGY, IMM16}), .clr(RST));
  Subtractor #(.width(6)) subtractor_1 (.a(OPCODE), .b(and_3_out), .out(subtractor_1_out));  // open: bin, bout
  Register #(.width(16)) A (.D(REG_IN), .en(decoder_2_out1), .clk(CLK), .Q(A_q), .clr(RST));
  Register #(.width(16)) u_B (.D(REG_IN), .en(decoder_2_out2), .clk(CLK), .Q(B_q), .clr(RST));
  Register #(.width(16)) C (.D(REG_IN), .en(decoder_2_out3), .clk(CLK), .Q(C_q), .clr(RST));
  Register #(.width(16)) D (.D(REG_IN), .en(decoder_2_out4), .clk(CLK), .Q(D_q), .clr(RST));
  // Probe on IMM16
  // Probe on subtractor_1_out[3:0]
  // Probe on B
  not not_2 (IS_ALU, OPCODE[4]);
  Multiplexer #(.width(16)) multiplexer_2 (.in0(REGY_OUT), .in1(IMM16), .out(B), .sel(OPCODE[2]));
  or or_3 (SEL1, IN_P, MOV);
  or or_4 (SEL0, LOAD, MOV);
  Multiplexer #(.select(5), .width(16)) multiplexer_3 (
    .in1(A_q), .in2(B_q), .in3(C_q), .in4(D_q), .out(REGX_OUT), .sel(REG_ADDR));  // open: in0, in5, in6, in7, in8, in9, in10, in11, in12, in13, in14, in15, in16, in17, in18, in19, in20, in21, in22, in23, in24, in25, in26, in27, in28, in29, in30, in31
  ALU alu_1 (
    .A(REGX_OUT), .B(B), .CIN(1'b0), .SEL(subtractor_1_out[3:0]), .OUTP(ALU_OUT), .COUT(COUT), .ZERO(ZERO));  // open: OVER, SIGN, HOUT, LT, GT, EQ
  or or_5 (REG_SET, SHRI, SHLI, ROTRI, ROTLI, ADD, SUB, ADDI, SUBI, LOAD, IN_P, MOV, MOVI);
  // Probe on REG_IN
  Multiplexer #(.select(3), .width(16)) multiplexer_4 (
    .in0(ALU_OUT), .in1(IMM16), .in2({16{1'b0}}), .in3(REG_OUT), .in4(RAM_OUT), .out(REG_IN),
    .sel({SEL0, SEL1, MOVI}));  // open: in5, in6, in7
  // Probe on {SEL0, SEL1, MOVI}
  Multiplexer #(.select(5), .width(16)) multiplexer_5 (
    .in1(A_q), .in2(B_q), .in3(B_q), .in4(D_q), .out(REGY_OUT), .sel(REGY));  // open: in0, in5, in6, in7, in8, in9, in10, in11, in12, in13, in14, in15, in16, in17, in18, in19, in20, in21, in22, in23, in24, in25, in26, in27, in28, in29, in30, in31

  // Other names for the same wires on the sheet: JMP[15:0] = IMM16; REGX[4:0] = REG_ADDR; SEL2 = MOVI

  // Notes on the sheet:
  //   contents of rom_1 (hex, n*v repeats v):
  //   60200003 60200003 0 0 30200003 0 20410001
endmodule

module comments (
);

  wire CLK, decoder_1_out8, decoder_1_out9, decoder_1_out14, decoder_1_out15, decoder_1_out16,
       decoder_1_out17, decoder_1_out18, decoder_1_out19, decoder_1_out20, decoder_1_out21, decoder_1_out22,
       decoder_1_out23, decoder_1_out24, decoder_1_out25, decoder_1_out26, decoder_1_out27, IS_ALU,
       j_k_ff_1_q, j_k_ff_2_q, PC_INC, RST, ST0, ST1, ST2, ST3, undriven;
  wire [4:0] bit_extender_1_out;
  wire [5:0] OPCODE;
  wire [15:0] enable16_1_outp, enable16_2_outp, IMM16, OUTP, REG_IN;

  Decoder #(.select(5)) decoder_1 (
    .out0(PC_INC), .out8(decoder_1_out8), .out9(decoder_1_out9), .out14(decoder_1_out14),
    .out15(decoder_1_out15), .out16(decoder_1_out16), .out17(decoder_1_out17), .out18(decoder_1_out18),
    .out19(decoder_1_out19), .out20(decoder_1_out20), .out21(decoder_1_out21), .out22(decoder_1_out22),
    .out23(decoder_1_out23), .out24(decoder_1_out24), .out25(decoder_1_out25), .out26(decoder_1_out26),
    .out27(decoder_1_out27), .sel(bit_extender_1_out), .en(1'b1));  // open: out1, out2, out3, out4, out5, out6, out7, out10, out11, out12, out13, out28, out29, out30, out31
  Bit_Extender #(.in_width(6), .out_width(5)) bit_extender_1 (.in(OPCODE), .out(bit_extender_1_out));
  // Buffer ADD has open pins: in=decoder_1_out8, out=open
  // Buffer SUB has open pins: in=decoder_1_out9, out=open
  // Buffer SHR has open pins: in=decoder_1_out14, out=open
  // Buffer SHL has open pins: in=decoder_1_out15, out=open
  // Buffer ROTR has open pins: in=decoder_1_out16, out=open
  // Buffer ROTL has open pins: in=decoder_1_out17, out=open
  // Buffer SUBI has open pins: in=decoder_1_out19, out=open
  // Buffer LOAD has open pins: in=decoder_1_out20, out=open
  // Buffer STORE has open pins: in=decoder_1_out21, out=open
  // Buffer INP has open pins: in=decoder_1_out22, out=open
  // Buffer OUTP has open pins: in=decoder_1_out23, out=open
  // Buffer JUMP has open pins: in=decoder_1_out24, out=open
  // Buffer JZ has open pins: in=decoder_1_out25, out=open
  // Buffer JN has open pins: in=decoder_1_out26, out=open
  // Buffer JC has open pins: in=decoder_1_out27, out=open
  Subtractor #(.width(2)) subtractor_1 (.b(2'b10));  // open: a, out, bin, bout
  and and_1 (ST1, j_k_ff_1_q, j_k_ff_2_q);
  J_K_Flip_Flop j_k_ff_1 (.J(1'b1), .K(1'b1), .clk(CLK), .Q(j_k_ff_1_q), .reset(RST));  // open: Qn, preset
  and and_2 (ST2, ~j_k_ff_1_q, j_k_ff_2_q);  // AND_Gate
  enable16 enable16_1 (.ENA(undriven), .I(IMM16), .OUTP(enable16_1_outp));
  enable16 enable16_2 (.ENA(IS_ALU), .I(OUTP), .OUTP(enable16_2_outp));
  J_K_Flip_Flop j_k_ff_2 (.J(1'b1), .K(1'b1), .clk(j_k_ff_1_q), .Q(j_k_ff_2_q), .reset(RST));  // open: Qn, preset
  and and_3 (ST3, j_k_ff_1_q, ~j_k_ff_2_q);  // AND_Gate
  and and_4 (ST0, ~ST1, ~ST2, ~ST3);  // AND_Gate
  assign REG_IN = enable16_1_outp | enable16_2_outp;  // OR_Gate or_1, 16 bits wide

  // Other names for the same wires on the sheet: PC_SET = PC_INC

  // Notes on the sheet:
  //   ADDI
  //   NOP
endmodule
